# Fritzing sketch multi-energy-monitor (saved by Fritzing 0.9.3b)
circuit board: 8.46667cm x 5.64444cm
breadboards: 1

parts:
  Componente1 = Arduino Nano (Rev3.0)
  TRS3 = Audio Jack (TRS) 3.5mm [package="4Ucon 08780 [THT]"]
  C3 = Electrolytic Capacitor [capacitance=10µF package="100 mil [THT, electrolytic]"]
  R1 = Resistor [tolerance=±5% resistance=10k package=THT]
  R2 = Resistor [tolerance=±5% resistance=10k package=THT]
  TRS4 = Audio Jack (TRS) 3.5mm [package="4Ucon 08780 [THT]"]
  C4 = Electrolytic Capacitor [capacitance=10µF package="100 mil [THT, electrolytic]"]
  R3 = Resistor [tolerance=±5% resistance=10k package=THT]
  R4 = Resistor [tolerance=±5% resistance=10k package=THT]
  TRS5 = Audio Jack (TRS) 3.5mm [package="4Ucon 08780 [THT]"]
  C5 = Electrolytic Capacitor [capacitance=10µF package="100 mil [THT, electrolytic]"]
  R5 = Resistor [tolerance=±5% resistance=10k package=THT]
  R6 = Resistor [tolerance=±5% resistance=10k package=THT]
  C6 = Electrolytic Capacitor [capacitance=10µF package="100 mil [THT, electrolytic]"]
  R7 = Resistor [tolerance=±5% resistance=100k package=THT]
  R8 = Resistor [tolerance=±5% resistance=10k package=THT]
  R9 = Resistor [tolerance=±5% resistance=10k package=THT]
  R10 = Resistor [tolerance=±5% resistance=10k package=THT]
  Power_plug1 = Power plug

nets:
  N1: Componente1.GND, C3.+, R1.Pin_0, C4.+, R4.Pin_0, C5.+, R6.Pin_0, R8.Pin_0
  N2: Componente1.5V, R2.Pin_1, R3.Pin_1, R5.Pin_1, C6.-, R9.Pin_0
  N3: Componente1.A3, R7.Pin_0, R10.Pin_0
  N4: Componente1.A2, TRS5.Tip
  N5: Componente1.A1, TRS4.Tip
  N6: Componente1.A0, TRS3.Tip
  N7: TRS3.Sleeve, C3.-, R1.Pin_1, R2.Pin_0
  N8: TRS4.Sleeve, C4.-, R3.Pin_0, R4.Pin_1
  N9: TRS5.Sleeve, C5.-, R5.Pin_0, R6.Pin_1
  N10: C6.+, R8.Pin_1, R9.Pin_1, R10.Pin_1, Power_plug1.GND
  N11: R7.Pin_1, Power_plug1.VCC
